# Fritzing sketch Temp Sensor (saved by Fritzing 0.7.4b)
breadboards: 1

parts:
  Arduino1 = Arduino
  LCD1 = LCD screen
  S1 = Pushbutton [package="[THT]"]
  R1 = Resistor [resistance=10k tolerance=±5% package=THT]
  T1 = LM35 Temperature Sensor [package="TO92 [THT]"]  # not connected

nets (from the schematic view):
  N1: Arduino1.GND, R1.Pin_1
  N2: Arduino1.D8, S1.Pin_1, S1.Pin_2, R1.Pin_0
  N3: Arduino1.D7, LCD1.RS
  N4: Arduino1.D6, LCD1.E
  N5: Arduino1.D5, LCD1.DB4
  N6: Arduino1.D4, LCD1.DB5
  N7: Arduino1.D3, LCD1.DB6
  N8: Arduino1.D2, LCD1.DB7
  N9: Arduino1.+5V, S1.Pin_3, S1.Pin_4
